// Logisim project CU.circ as structural Verilog: 2 circuits, main circuit main
module main (
  input  [15:0] Instruction
);

  PARSER parser_1 ();  // open: Instruction, COMMAND, A1, A2, A3, M1, M2
endmodule

// PAR
module PARSER (
  input  [15:0] Instruction,
  output [3:0] COMMAND,
  output [2:0] A1,
  output [2:0] A2,
  output [2:0] A3,
  output [7:0] M1,
  output [7:0] M2
);


  assign A1 = Instruction[6:4];
  assign A2 = Instruction[9:7];
  assign A3 = Instruction[12:10];
  assign COMMAND = Instruction[3:0];
  assign M1 = Instruction[11:4];
  assign M2 = Instruction[14:7];
endmodule
