// Logisim project procesor.circ as structural Verilog
module Procesor (
  output [3:0] ZCOP,
  output [7:0] out_2,
  output [7:0] out_3
);

  wire CLK_out, flags_1_p1, main_1_p3, main_2_p2, main_2_p3, main_2_p4, main_2_p5, main_2_p6, main_2_p7,
       not_1_out, not_2_out, not_3_out, registers_1_p2, registers_1_p9, registers_1_p10;
  wire [7:0] main_1_p5, multiplexer_1_out, ram_2_data, undriven;
  wire [15:0] ram_1_data;

  Clock CLK (.out(CLK_out));
  // PC_main main_1: pin names not known; wires that end beside it: CLK_out, out_2, main_1_p3, ZCOP[3], main_1_p5
  not not_1 (not_1_out, 1'b1);
  // CU_main main_2: pin names not known; wires that end beside it: main_1_p3, main_2_p2, main_2_p3, main_2_p4, main_2_p5, main_2_p6, main_2_p7
  RAM #(.dataWidth(16), .bus("separate")) ram_1 (
    .addr(main_1_p5), .data(ram_1_data), .str(not_1_out), .clk(CLK_out), .ld(1'b1));  // open: din, sel, clr
  not not_2 (not_2_out, main_2_p3);
  Multiplexer #(.width(8)) multiplexer_1 (
    .in0(out_2), .in1(ram_2_data), .out(multiplexer_1_out), .sel(main_2_p4));  // open: en
  RAM #(.bus("separate")) ram_2 (
    .addr(undriven), .din(out_3), .data(ram_2_data), .str(main_2_p3), .clk(CLK_out), .ld(not_2_out));  // open: sel, clr
  not not_3 (not_3_out, main_2_p3);
  // Registers registers_1: pin names not known; wires that end beside it: multiplexer_1_out, registers_1_p2, main_2_p5, main_2_p6, CLK_out, main_2_p2, not_3_out, out_3, registers_1_p9, registers_1_p10, main_2_p7
  // Flags flags_1: pin names not known; wires that end beside it: flags_1_p1, CLK_out, ZCOP[0], ZCOP[1], ZCOP[2], ZCOP[3]
endmodule
